// Logisim project contadorNumerosPares.circ as structural Verilog: 1 circuit, main circuit main
module main (
);

  wire and_1_out, clock_1_out, not_1_out, Q1, Q2, Q3, Q4;

  Clock clock_1 (.out(clock_1_out));
  J_K_Flip_Flop j_k_ff_1 (.J(1'b0), .K(1'b0), .clk(clock_1_out), .Q(Q4));  // open: Qn, preset, reset
  not not_1 (not_1_out, Q1);
  J_K_Flip_Flop j_k_ff_2 (.J(not_1_out), .K(1'b1), .clk(clock_1_out), .Q(Q3));  // open: Qn, preset, reset
  Hex_Digit_Display hex_digit_display_1 (.value({Q1, Q2, Q3, Q4}));  // open: dp
  J_K_Flip_Flop j_k_ff_3 (.J(Q3), .K(Q3), .clk(clock_1_out), .Q(Q2));  // open: Qn, preset, reset
  and and_1 (and_1_out, Q3, Q2);
  J_K_Flip_Flop j_k_ff_4 (.J(and_1_out), .K(1'b1), .clk(clock_1_out), .Q(Q1));  // open: Qn, preset, reset
endmodule
