// Logisim project ex01.circ as structural Verilog: 4 circuits, main circuit main
module main (
);

  wire button_1_out;

  Button button_1 (.out(button_1_out));
  LED led_1 ();  // open: in
  timer5 timer5_1 (.I(button_1_out));  // open: O
  timer8 timer8_1 ();  // open: I, O
  timer4 timer4_1 ();  // open: I, O
endmodule

module timer5 (
  input  I,
  output O
);

  wire and_1_out, and_2_out, clock_1_out, is_5, j_k_ff_2_q, j_k_ff_3_q, j_k_ff_4_q, reset;

  J_K_Flip_Flop j_k_ff_1 (.Q(O), .preset(I), .reset(is_5));  // open: J, K, clk, Qn
  Clock clock_1 (.out(clock_1_out));
  not not_1 (reset, O);
  and and_1 (and_1_out, O, clock_1_out);
  J_K_Flip_Flop j_k_ff_2 (.J(1'b1), .K(1'b1), .clk(and_1_out), .Q(j_k_ff_2_q), .reset(reset));  // open: Qn, preset
  J_K_Flip_Flop j_k_ff_3 (
    .J(j_k_ff_2_q), .K(j_k_ff_2_q), .clk(and_1_out), .Q(j_k_ff_3_q), .reset(reset));  // open: Qn, preset
  and and_2 (and_2_out, j_k_ff_2_q, j_k_ff_3_q);
  J_K_Flip_Flop j_k_ff_4 (
    .J(and_2_out), .K(and_2_out), .clk(and_1_out), .Q(j_k_ff_4_q), .reset(reset));  // open: Qn, preset
  and and_3 (is_5, j_k_ff_2_q, j_k_ff_4_q);
endmodule

module timer8 (
  input  I,
  output O
);

  wire and_1_out, and_2_out, clock_1_out, is_8, j_k_ff_2_q, j_k_ff_3_q, j_k_ff_4_q, reset;

  J_K_Flip_Flop j_k_ff_1 (.Q(O), .preset(I), .reset(is_8));  // open: J, K, clk, Qn
  and and_1 (and_1_out, O, clock_1_out);
  Clock clock_1 (.out(clock_1_out));
  not not_1 (reset, O);
  J_K_Flip_Flop j_k_ff_2 (.J(1'b1), .K(1'b1), .clk(and_1_out), .Q(j_k_ff_2_q), .reset(reset));  // open: Qn, preset
  J_K_Flip_Flop j_k_ff_3 (
    .J(j_k_ff_2_q), .K(j_k_ff_2_q), .clk(and_1_out), .Q(j_k_ff_3_q), .reset(reset));  // open: Qn, preset
  and and_2 (and_2_out, j_k_ff_2_q, j_k_ff_3_q);
  J_K_Flip_Flop j_k_ff_4 (
    .J(and_2_out), .K(and_2_out), .clk(and_1_out), .Q(j_k_ff_4_q), .reset(reset));  // open: Qn, preset
  and and_3 (is_8, j_k_ff_2_q, j_k_ff_3_q, j_k_ff_4_q);
endmodule

module timer4 (
  input  I,
  output O
);

  wire and_1_out, and_2_out, clock_1_out, is_4, j_k_ff_2_q, j_k_ff_3_q, reset;

  J_K_Flip_Flop j_k_ff_1 (.Q(O), .preset(I), .reset(is_4));  // open: J, K, clk, Qn
  not not_1 (reset, O);
  and and_1 (and_1_out, O, clock_1_out);
  Clock clock_1 (.out(clock_1_out));
  J_K_Flip_Flop j_k_ff_2 (.J(1'b1), .K(1'b1), .clk(and_1_out), .Q(j_k_ff_2_q), .reset(reset));  // open: Qn, preset
  J_K_Flip_Flop j_k_ff_3 (
    .J(j_k_ff_2_q), .K(j_k_ff_2_q), .clk(and_1_out), .Q(j_k_ff_3_q), .reset(reset));  // open: Qn, preset
  and and_2 (and_2_out, j_k_ff_2_q, j_k_ff_3_q);
  J_K_Flip_Flop j_k_ff_4 (.J(and_2_out), .K(and_2_out), .clk(and_1_out), .Q(is_4), .reset(reset));  // open: Qn, preset
endmodule
