// Logisim project listaExercicios.circ as structural Verilog
module ex01 (
);

  wire and_1_out, clock_1_out, ex06_1_a, ex06_1_b, ex06_1_c, ex06_1_d, ex06_1_e, ex06_1_f, ex06_1_g,
       j_k_ff_1_qn, j_k_ff_2_qn, j_k_ff_3_qn, Q0, Q1, Q2, Q3;

  Clock clock_1 (.out(clock_1_out));
  J_K_Flip_Flop j_k_ff_1 (
    .J(1'b1), .K(1'b1), .clk(clock_1_out), .Q(Q0), .Qn(j_k_ff_1_qn), .reset(and_1_out));  // open: preset
  J_K_Flip_Flop j_k_ff_2 (
    .J(1'b1), .K(1'b1), .clk(j_k_ff_1_qn), .Q(Q1), .Qn(j_k_ff_2_qn), .reset(and_1_out));  // open: preset
  and and_1 (and_1_out, Q1, Q3);
  J_K_Flip_Flop j_k_ff_3 (
    .J(1'b1), .K(1'b1), .clk(j_k_ff_2_qn), .Q(Q2), .Qn(j_k_ff_3_qn), .reset(and_1_out));  // open: preset
  J_K_Flip_Flop j_k_ff_4 (.J(1'b1), .K(1'b1), .clk(j_k_ff_3_qn), .Q(Q3), .reset(and_1_out));  // open: Qn, preset
  ex06 ex06_1 (
    .B3(Q3), .B2(Q2), .B1(Q1), .B0(Q0), .g(ex06_1_g), .a(ex06_1_a), .b(ex06_1_b), .c(ex06_1_c), .d(ex06_1_d),
    .e(ex06_1_e), .f(ex06_1_f));
  _7_Segment_Display #(.decimalPoint("false")) u_7_segment_display_1 (
    .g(ex06_1_g), .f(ex06_1_f), .a(ex06_1_a), .b(ex06_1_b), .e(ex06_1_e), .d(ex06_1_d), .c(ex06_1_c));
endmodule

module ex02 (
  input  in_1
);

  wire and_1_out, and_2_out, and_3_out, and_4_out, clock_1_out, ex06_1_a, ex06_1_b, ex06_1_c, ex06_1_d,
       ex06_1_e, ex06_1_f, ex06_1_g, J1, J2, not_1_out, not_2_out, not_3_out, not_4_out, not_5_out, Q0, Q1,
       Q2;

  Clock clock_1 (.out(clock_1_out));
  J_K_Flip_Flop j_k_ff_1 (.J(1'b1), .K(1'b1), .clk(clock_1_out), .Q(Q0));  // open: Qn, preset, reset
  not not_1 (not_1_out, in_1);
  and and_1 (and_1_out, not_1_out, not_2_out);
  not not_2 (not_2_out, Q0);
  and and_2 (and_2_out, in_1, Q0);
  J_K_Flip_Flop j_k_ff_2 (.J(J1), .K(J1), .clk(clock_1_out), .Q(Q1));  // open: Qn, preset, reset
  or or_1 (J1, and_1_out, and_2_out);
  J_K_Flip_Flop j_k_ff_3 (.J(J2), .K(J2), .clk(clock_1_out), .Q(Q2));  // open: Qn, preset, reset
  not not_3 (not_3_out, in_1);
  not not_4 (not_4_out, Q0);
  not not_5 (not_5_out, Q1);
  and and_3 (and_3_out, not_3_out, not_4_out, not_5_out);
  and and_4 (and_4_out, in_1, Q0, Q1);
  or or_2 (J2, and_3_out, and_4_out);
  ex06 ex06_1 (
    .B3(1'b0), .B2(Q2), .B1(Q1), .B0(Q0), .g(ex06_1_g), .a(ex06_1_a), .b(ex06_1_b), .c(ex06_1_c),
    .d(ex06_1_d), .e(ex06_1_e), .f(ex06_1_f));
  _7_Segment_Display #(.decimalPoint("false")) u_7_segment_display_1 (
    .g(ex06_1_g), .f(ex06_1_f), .a(ex06_1_a), .b(ex06_1_b), .e(ex06_1_e), .d(ex06_1_d), .c(ex06_1_c));

  // Other names for the same wires on the sheet: K1 = J1; K2 = J2; U_D = in_1
endmodule

module ex06 (
  input  B3,
  input  B2,
  input  B1,
  input  B0,
  output a,
  output b,
  output c,
  output d,
  output e,
  output f,
  output g
);

  wire and_1_out, and_2_out, and_3_out, and_4_out, and_5_out, and_6_out, and_7_out, not_1_out, not_2_out,
       not_3_out, or_1_out, or_2_out, xnor_1_out, xnor_2_out, xor_1_out;

  not not_1 (not_1_out, B2);
  not not_2 (not_2_out, B1);
  not not_3 (not_3_out, B0);
  xnor xnor_1 (xnor_1_out, B2, B0);
  xnor xnor_2 (xnor_2_out, B1, B0);
  and and_1 (and_1_out, B1, not_3_out);
  and and_2 (and_2_out, not_1_out, B1);
  and and_3 (and_3_out, not_1_out, not_3_out);
  and and_4 (and_4_out, B2, not_2_out, B0);
  or or_1 (or_1_out, not_1_out, B1);
  and and_5 (and_5_out, not_2_out, not_3_out);
  and and_6 (and_6_out, B2, or_2_out);
  or or_2 (or_2_out, not_2_out, not_3_out);
  xor xor_1 (xor_1_out, B2, B1);
  and and_7 (and_7_out, B1, not_3_out);
  or or_3 (a, B3, B1, xnor_1_out);
  or or_4 (b, not_1_out, xnor_2_out);
  or or_5 (c, B2, not_2_out, B0);
  or or_6 (d, B3, and_1_out, and_2_out, and_3_out, and_4_out);
  and and_8 (e, not_3_out, or_1_out);
  or or_7 (f, B3, and_5_out, and_6_out);
  or or_8 (g, B3, xor_1_out, and_7_out);
endmodule
